// Logisim project Basic Computer.circ as structural Verilog: 1 circuit, main circuit main
module main (
  input  Should_be_1,
  input  Should_be_1_2,
  input  in_3,
  input  [2:0] Should_be_100,
  input  Should_be_1_3,
  input  in_6,
  input  in_7,
  input  [3:0] Should_be_1111,
  input  [3:0] Should_be_0010,
  input  [15:0] in_10,
  output out_11,
  output out_12
);

  wire bitselector_2_out, bitselector_3_out, clock_1_out, CLR_SC_out, comparator_1_eq, D0T4_out, D0T5_out,
       D1T4_out, D1T5_out, D2T4_out, D2T5_out, D3T4_out, D4T4_out, D5T4_out, D5T5_out, D7_I_prime_T3_out,
       d_ff_1_q, decoder_1_out0, decoder_1_out1, decoder_1_out2, decoder_1_out3, decoder_1_out4,
       decoder_1_out5, decoder_2_out0, decoder_2_out1, decoder_2_out2, decoder_2_out3, decoder_2_out4,
       decoder_2_out5, decoder_2_out7, INC_PC_out, LD_AC_out, LD_AR_out, LD_DR_out, not_2_out,
       rB2AC_prime_out, READ_out;
  wire [2:0] bitselector_1_out, priority_encoder_1_p1, priority_encoder_2_p1;
  wire [3:0] SC_q;
  wire [11:0] AR_q, bit_extender_1_out, bit_extender_2_out, PC_q;
  wire [15:0] AC_q, adder_1_out, and_1_out, bit_extender_3_out, bit_extender_4_out, DR_q, IR_q,
       multiplexer_1_out, multiplexer_2_out, not_1_out, or_1_out, ram_1_data, subtractor_1_out, TR_q,
       xor_1_out;

  Adder #(.width(16)) adder_1 (.a(AC_q), .b(DR_q), .out(adder_1_out), .cin(in_6), .cout(out_11));
  Subtractor #(.width(16)) subtractor_1 (.a(AC_q), .b(DR_q), .out(subtractor_1_out), .bin(in_7), .bout(out_12));
  assign and_1_out = AC_q & DR_q;  // AND_Gate and_1, 16 bits wide
  assign or_1_out = AC_q | DR_q;  // OR_Gate or_1, 16 bits wide
  assign xor_1_out = AC_q ^ DR_q;  // XOR_Gate xor_1, 16 bits wide
  assign not_1_out = ~AC_q;  // NOT_Gate not_1, 16 bits wide
  Multiplexer #(.select(3), .width(16)) multiplexer_1 (
    .in0(adder_1_out), .in1(subtractor_1_out), .in2(DR_q), .in3(and_1_out), .in4(or_1_out), .in5(xor_1_out),
    .in6(not_1_out), .out(multiplexer_1_out), .sel(priority_encoder_1_p1));  // open: in7, en
  and D2T5 (D2T5_out, decoder_2_out2, decoder_1_out5);
  and D5T5 (D5T5_out, decoder_2_out5, decoder_1_out5);
  and D1T5 (D1T5_out, decoder_2_out1, decoder_1_out5);
  and D0T5 (D0T5_out, decoder_1_out5, decoder_2_out0);
  Clock clock_1 (.out(clock_1_out));
  or LD_AC (LD_AC_out, D2T5_out, D5T5_out, D1T5_out, D0T5_out);
  and D2T4 (D2T4_out, decoder_2_out2, decoder_1_out4);
  and D1T4 (D1T4_out, decoder_2_out1, decoder_1_out4);
  and D0T4 (D0T4_out, decoder_2_out0, decoder_1_out4);
  or LD_AR (LD_AR_out, decoder_1_out0, decoder_1_out2);
  and D5T4 (D5T4_out, decoder_2_out5, decoder_1_out4);
  or INC_PC (INC_PC_out, rB2AC_prime_out, decoder_1_out1);
  or READ (READ_out, decoder_1_out1, D5T4_out, D2T4_out, D1T4_out, D0T4_out);
  or LD_DR (LD_DR_out, D5T4_out, D2T4_out, D1T4_out, D0T4_out);
  D_Flip_Flop d_ff_1 (.clk(clock_1_out), .D(CLR_SC_out), .Q(d_ff_1_q));  // open: Qn, preset, en, reset
  Bit_Extender #(.in_width(16), .out_width(12)) bit_extender_1 (.in(multiplexer_2_out), .out(bit_extender_1_out));
  and rB2AC_prime (rB2AC_prime_out, D7_I_prime_T3_out, bitselector_2_out, comparator_1_eq);
  Register #(.width(16)) AC (.D(multiplexer_1_out), .en(LD_AC_out), .Q(AC_q), .clk(clock_1_out));  // open: clr
  Register #(.width(16)) DR (.D(multiplexer_2_out), .en(LD_DR_out), .Q(DR_q), .clk(clock_1_out));  // open: clr
  Register #(.width(12)) AR (.D(bit_extender_1_out), .en(LD_AR_out), .Q(AR_q), .clk(clock_1_out));  // open: clr
  Bit_Extender #(.in_width(16), .out_width(12)) bit_extender_2 (.in(multiplexer_2_out), .out(bit_extender_2_out));
  Register #(.width(16)) TR (.D(multiplexer_2_out), .en(in_3), .Q(TR_q), .clk(clock_1_out));  // open: clr
  Counter #(.width(4), .max('hf)) SC (
    .count(Should_be_1_3), .Q(SC_q), .clk(clock_1_out), .clr(d_ff_1_q));  // open: load, D, carry
  or CLR_SC (CLR_SC_out, D0T5_out, D1T5_out, D2T5_out, D5T5_out, D4T4_out, D7_I_prime_T3_out, D3T4_out);
  RAM #(.addrWidth(12), .dataWidth(16), .bus("separate")) ram_1 (
    .addr(AR_q), .din(multiplexer_2_out), .data(ram_1_data), .str(D3T4_out), .clk(clock_1_out), .ld(READ_out));  // open: sel, clr
  Counter #(.width(12), .max('hfff)) PC (
    .load(D4T4_out), .D(bit_extender_2_out), .count(INC_PC_out), .Q(PC_q), .clk(clock_1_out));  // open: carry, clr
  Register #(.width(16)) IR (.D(multiplexer_2_out), .en(decoder_1_out1), .Q(IR_q), .clk(clock_1_out));  // open: clr
  BitSelector #(.width(16), .group(3)) bitselector_1 (.in(IR_q), .out(bitselector_1_out), .sel(Should_be_100));
  Decoder #(.select(4)) decoder_1 (
    .out0(decoder_1_out0), .out1(decoder_1_out1), .out2(decoder_1_out2), .out3(decoder_1_out3),
    .out4(decoder_1_out4), .out5(decoder_1_out5), .sel(SC_q));  // open: out6, out7, out8, out9, out10, out11, out12, out13, out14, out15, en
  assign bit_extender_3_out = {{4{1'b0}}, AR_q};  // Bit_Extender bit_extender_3
  Decoder #(.select(3)) decoder_2 (
    .out0(decoder_2_out0), .out1(decoder_2_out1), .out2(decoder_2_out2), .out3(decoder_2_out3),
    .out4(decoder_2_out4), .out5(decoder_2_out5), .out7(decoder_2_out7), .sel(bitselector_1_out));  // open: out6, en
  and D4T4 (D4T4_out, decoder_1_out4, decoder_2_out4);
  and D7_I_prime_T3 (D7_I_prime_T3_out, decoder_1_out3, not_2_out, decoder_2_out7);
  Comparator #(.width(16)) comparator_1 (.a(AC_q), .b(in_10), .eq(comparator_1_eq));  // open: gt, lt
  assign bit_extender_4_out = {{4{1'b0}}, PC_q};  // Bit_Extender bit_extender_4
  and D3T4 (D3T4_out, decoder_1_out4, decoder_2_out3);
  BitSelector #(.width(16)) bitselector_2 (.in(IR_q), .out(bitselector_2_out), .sel(Should_be_0010));
  Multiplexer #(.select(3), .width(16)) multiplexer_2 (
    .in0(AC_q), .in1(DR_q), .in2(TR_q), .in3(bit_extender_3_out), .in4(ram_1_data), .in5(bit_extender_4_out),
    .in6(IR_q), .out(multiplexer_2_out), .sel(priority_encoder_2_p1));  // open: in7, en
  not not_2 (not_2_out, bitselector_3_out);
  BitSelector #(.width(16)) bitselector_3 (.in(IR_q), .out(bitselector_3_out), .sel(Should_be_1111));
  // Priority_Encoder priority_encoder_1: pin names not known; wires that end beside it: priority_encoder_1_p1, Should_be_1, D1T5_out, D5T5_out, D2T5_out, D0T5_out
  // Priority_Encoder priority_encoder_2: pin names not known; wires that end beside it: priority_encoder_2_p1, Should_be_1_2, D3T4_out, D4T4_out, READ_out, decoder_1_out0, decoder_1_out2

  // Notes on the sheet:
  //   Decode(12~14) IR
  //   IF (AC=0)
  //   IR(2)
  //   I'
  //   ALU Control
  //   Bus Control
endmodule
